// Logisim project ALU.circ as structural Verilog: 1 circuit, main circuit ALU
module ALU (
  input  [3:0] S,
  input  [31:0] X,
  input  [31:0] Y,
  output [31:0] R
);

  wire [0:0] comparator_1_eq, comparator_1_gt, comparator_1_lt, not_1_out, or_1_out, or_2_out;
  wire [31:0] adder_1_out, divider_1_out, divider_1_rem, multiplier_1_out, negator_1_out, subtractor_1_out;

  Negator #(.width(32)) negator_1 (.in(X), .out(negator_1_out));
  Adder #(.width(32)) adder_1 (.a(X), .b(Y), .out(adder_1_out));  // open: cin, cout
  Subtractor #(.width(32)) subtractor_1 (.a(X), .b(Y), .out(subtractor_1_out));  // open: bin, bout
  Multiplier #(.width(32)) multiplier_1 (.a(X), .b(Y), .out(multiplier_1_out));  // open: cin, cout
  Divider #(.width(32)) divider_1 (.a(X), .b(Y), .out(divider_1_out), .rem(divider_1_rem));  // open: upper
  Comparator #(.width(32)) comparator_1 (
    .a(X), .b(Y), .gt(comparator_1_gt[0]), .eq(comparator_1_eq[0]), .lt(comparator_1_lt[0]));
  not not_1 (not_1_out[0], comparator_1_eq[0]);
  or or_1 (or_1_out[0], comparator_1_lt[0], comparator_1_eq[0]);
  or or_2 (or_2_out[0], comparator_1_gt[0], comparator_1_eq[0]);
  Multiplexer #(.select(4), .width(32)) multiplexer_1 (
    .in0({32{1'b0}}), .in1(negator_1_out), .in2(adder_1_out), .in3(subtractor_1_out), .in4(multiplier_1_out),
    .in5(divider_1_out), .in6({{31{1'b0}}, X[0]}), .in7(divider_1_rem),
    .in8({{31{1'b0}}, comparator_1_eq[0]}), .in9({{31{1'b0}}, not_1_out[0]}),
    .in10({{31{1'b0}}, comparator_1_lt[0]}), .in11({{31{1'b0}}, or_1_out[0]}),
    .in12({{31{1'b0}}, comparator_1_gt[0]}), .in13({{31{1'b0}}, or_2_out[0]}), .in14({32{1'b0}}),
    .in15({32{1'b0}}), .out(R), .sel(S));  // open: en
endmodule
