// Logisim project CPU.circ as structural Verilog: 1 circuit, main circuit main
// Started
module main (
);

  wire ALUXWE, and_1_out, BaseInSlct, BaseWE, BranchSlct, CLInSlct, Clk, clock_1_out, CLWE, comparator_1_eq,
       DAInSlct, DspAInSlct, DspDInSlct, DspWE, InstRegWE, j_k_ff_1_qn, MemRE, MemWE, MICInSlct, MICWE,
       or_1_out, OutputWE, PC1, PCWE, TopWE;
  wire [1:0] PCInSlct, TopInSlct;
  wire [2:0] DDInSlct;
  wire [3:0] TopOutOffset;
  wire [7:0] adder_2_out, CL, DiffCL, InstL, InstOP, multiplexer_2_out, multiplexer_5_out;
  wire [15:0] adder_1_out, adder_3_out, adder_4_out, adder_5_out, adder_6_out, adder_7_out, Base,
       bit_extender_1_out, DspOut, InstM, MIC, multiplexer_1_out, multiplexer_3_out, multiplexer_4_out,
       multiplexer_6_out, multiplexer_7_out, multiplexer_8_out, multiplexer_9_out, multiplexer_11_out, PC,
       subtractor_1_out, Top;
  wire [31:0] ALUOut, ALUX_q, bit_extender_2_out, bit_extender_3_out, bit_extender_4_out, bit_extender_5_out,
       bit_extender_6_out, DReg, multiplexer_10_out, Output, ram_2_data, rom_1_data;
  wire [31:29] rom_2_data;

  // Probe on Clk
  // Probe on BranchSlct
  // Probe on PCInSlct
  // Probe on PCWE
  // Probe on InstRegWE
  // Probe on CLInSlct
  // Probe on CLWE
  // Probe on DspAInSlct
  // Probe on DspDInSlct
  // Probe on DspWE
  // Probe on TopOutOffset
  // Probe on DAInSlct
  // Probe on DDInSlct
  // Probe on MemWE
  // Probe on MemRE
  // Probe on ALUXWE
  // Probe on TopInSlct
  // Probe on TopWE
  // Probe on BaseInSlct
  // Probe on BaseWE
  // Probe on MICInSlct
  // Probe on MICWE
  Comparator #(.width(32)) comparator_1 (.a(DReg), .b({32{1'b0}}), .eq(comparator_1_eq));  // open: gt, lt
  and and_1 (and_1_out, comparator_1_eq, BranchSlct);
  Adder #(.width(16)) adder_1 (.a(PC), .b(16'h1), .out(adder_1_out));  // open: cin, cout
  Adder adder_2 (.a(DiffCL), .b(8'h1), .out(adder_2_out));  // open: cin, cout
  Adder #(.width(16)) adder_3 (.a(Top), .b(16'h1), .out(adder_3_out));  // open: cin, cout
  Subtractor #(.width(16)) subtractor_1 (.a(Top), .b(16'h1), .out(subtractor_1_out));  // open: bin, bout
  Adder #(.width(16)) adder_4 (.a(Top), .b(InstM), .out(adder_4_out));  // open: cin, cout
  Register #(.width(32)) ALUX (.D(DReg), .en(ALUXWE), .Q(ALUX_q), .clk(Clk));  // open: clr
  Multiplexer #(.width(16)) multiplexer_1 (
    .in0(adder_1_out), .in1(InstM), .out(multiplexer_1_out), .sel(and_1_out));  // open: en
  Multiplexer #(.width(8)) multiplexer_2 (
    .in0(DReg[7:0]), .in1(adder_2_out), .out(multiplexer_2_out), .sel(CLInSlct));  // open: en
  Multiplexer #(.select(2), .width(16)) multiplexer_3 (
    .in0(adder_3_out), .in1(subtractor_1_out), .in2(adder_4_out), .in3(Base), .out(multiplexer_3_out),
    .sel(TopInSlct));  // open: en
  ALU alu_1 (.X(DReg), .Y(ALUX_q), .R(ALUOut), .S(InstM[3:0]));
  // Probe on PC
  // Probe on MIC
  // Probe on InstOP
  // Probe on InstL
  // Probe on InstM
  J_K_Flip_Flop j_k_ff_1 (.J(PC1), .clk(clock_1_out), .K(1'b0), .Qn(j_k_ff_1_qn));  // open: Q, preset, en, reset
  or or_1 (or_1_out, PC1, j_k_ff_1_qn);
  Multiplexer #(.select(2), .width(16)) multiplexer_4 (
    .in0(multiplexer_1_out), .in1(InstM), .in2(DReg[15:0]), .out(multiplexer_4_out), .sel(PCInSlct));  // open: in3, en
  Register #(.width(16)) u_PC (.D(multiplexer_4_out), .en(PCWE), .Q(PC), .clk(Clk));  // open: clr
  Register u_CL (.D(multiplexer_2_out), .en(CLWE), .Q(CL), .clk(Clk));  // open: clr
  Register #(.width(16)) u_Top (.D(multiplexer_3_out), .en(TopWE), .Q(Top), .clk(Clk));  // open: clr
  assign Clk = or_1_out ? clock_1_out : 1'bz;  // Controlled_Buffer controlled_buffer_1
  Clock clock_1 (.out(clock_1_out));
  Subtractor subtractor_2 (.a(CL), .b(InstL), .out(DiffCL));  // open: bin, bout
  // Probe on Top
  // Probe on Base
  // Probe on DReg
  // Probe on CL
  // Probe on DspOut
  // Probe on Output
  ROM #(.addrWidth(16), .dataWidth(32)) rom_1 (.addr(PC), .data(rom_1_data));  // open: sel
  Multiplexer #(.width(8)) multiplexer_5 (
    .in0(CL), .in1(DiffCL), .out(multiplexer_5_out), .sel(DspAInSlct));  // open: en
  Multiplexer #(.width(16)) multiplexer_6 (
    .in0(Top), .in1(DReg[15:0]), .out(multiplexer_6_out), .sel(DspDInSlct));  // open: en
  Register #(.width(32)) InstReg (.D(rom_1_data), .en(InstRegWE), .Q({InstOP, InstL, InstM}), .clk(Clk));  // open: clr
  Multiplexer #(.width(16)) multiplexer_7 (
    .in0(DReg[15:0]), .in1(Top), .out(multiplexer_7_out), .sel(BaseInSlct));  // open: en
  Register #(.width(32)) OutputReg (.D(DReg), .en(OutputWE), .Q(Output), .clk(Clk));  // open: clr
  Register #(.width(16)) u_Base (.D(multiplexer_7_out), .en(BaseWE), .Q(Base), .clk(Clk));  // open: clr
  RAM #(.dataWidth(16), .bus("separate")) ram_1 (
    .addr(multiplexer_5_out), .din(multiplexer_6_out), .data(DspOut), .str(DspWE), .clk(Clk), .ld(1'b1));  // open: sel, clr
  or or_2 (PC1, PC[0], PC[1], PC[2], PC[3], PC[4], PC[5], PC[6], PC[7], PC[8], PC[9], PC[10], PC[11], PC[12], PC[13], PC[14], PC[15], PC[15]);
  assign bit_extender_1_out = {{12{TopOutOffset[3]}}, TopOutOffset};  // Bit_Extender bit_extender_1
  assign bit_extender_2_out = {{16{InstM[15]}}, InstM};  // Bit_Extender bit_extender_2
  assign bit_extender_3_out = {{24{1'b0}}, CL};  // Bit_Extender bit_extender_3
  assign bit_extender_4_out = {{16{1'b0}}, DspOut};  // Bit_Extender bit_extender_4
  assign bit_extender_5_out = {{16{1'b0}}, Base};  // Bit_Extender bit_extender_5
  assign bit_extender_6_out = {{16{1'b0}}, PC};  // Bit_Extender bit_extender_6
  Adder #(.width(16)) adder_5 (.a(DspOut), .b(InstM), .out(adder_5_out));  // open: cin, cout
  Adder #(.width(16)) adder_6 (.a(bit_extender_1_out), .b(Top), .out(adder_6_out));  // open: cin, cout
  Adder #(.width(16)) adder_7 (.a(MIC), .b(16'h1), .out(adder_7_out));  // open: cin, cout
  Multiplexer #(.select(4), .width(16)) multiplexer_8 (
    .in0(16'h1), .in1(16'h3), .in2(16'h6), .in3(16'h8), .in4(16'ha), .in5(16'hf), .in6(16'h15), .in7(16'h17),
    .in8(16'h19), .in9({16{1'b0}}), .in10(16'h1c), .out(multiplexer_8_out), .sel(InstOP[3:0]));  // open: in11, in12, in13, in14, in15, en
  Multiplexer #(.width(16)) multiplexer_9 (
    .in0(adder_5_out), .in1(adder_6_out), .out(multiplexer_9_out), .sel(DAInSlct));  // open: en
  Multiplexer #(.select(3), .width(32)) multiplexer_10 (
    .in0(DReg), .in1(ALUOut), .in2(bit_extender_2_out), .in3(bit_extender_3_out), .in4(bit_extender_4_out),
    .in5(bit_extender_5_out), .in6(bit_extender_6_out), .out(multiplexer_10_out), .sel(DDInSlct));  // open: in7, en
  Multiplexer #(.width(16)) multiplexer_11 (
    .in0(adder_7_out), .in1(multiplexer_8_out), .out(multiplexer_11_out), .sel(MICInSlct));  // open: en
  Register #(.width(16), .trigger("falling")) u_MIC (
    .D(multiplexer_11_out), .en(MICWE), .Q(MIC), .clk(Clk));  // open: clr
  RAM #(.addrWidth(16), .dataWidth(32), .bus("separate")) ram_2 (
    .addr(multiplexer_9_out), .din(multiplexer_10_out), .data(ram_2_data), .str(MemWE), .clk(Clk), .ld(MemRE));  // open: sel, clr
  Register #(.width(32)) u_DReg (.D(ram_2_data), .en(MemRE), .Q(DReg), .clk(Clk));  // open: clr
  ROM #(.addrWidth(16), .dataWidth(32)) rom_2 (
    .addr(MIC),
    .data({rom_2_data, OutputWE, MICWE, MICInSlct, BaseWE, BaseInSlct, TopWE, TopInSlct, ALUXWE, MemRE, MemWE, DDInSlct, DAInSlct, TopOutOffset, DspWE, DspDInSlct, DspAInSlct, CLWE, CLInSlct, InstRegWE, PCWE, PCInSlct, BranchSlct}));  // open: sel

  // Notes on the sheet:
  //   contents of rom_1 (hex, n*v repeats v):
  //   700002d 7000002 6000005 200fffe 200ffff 1000005 3000004 200fffe 200ffff 2000004 1000004 1000003
  //   3010006 5000000 700000f 6000005 200fffe 200ffff 100000a 800001a 200fffe 3000004 200ffff 300fffe
  //   2000004 300ffff 200ffff 0 1000009 8000026 200fffe 200ffff 4010001 600fffe 200ffff 2010006 401000e
  //   600fffe 200ffff 0 1000008 800002c 200fffe 3010007 5000000 6000008 3c 3000004 48 3000005 2000004
  //   2000005 400000e 600fffe 2000007 a000000 5000000
  //   contents of rom_2 (hex, n*v repeats v):
  //   c000010 8054008 c800010 8a87c08 8187c00 c04fc10 8080088 c844010 8a87c08 c240090 825c068 8264600
  //   b26c800 8074c0a c000010 8e00000 8e84c00 808480c a084404 8084300 c000050 8c00008 c000010 800000a
  //   c000010 8a87c00 8000009 c000010 8a87c08 1c000010
endmodule
