// Logisim project MicroInstructionGenerator.circ as structural Verilog: 1 circuit, main circuit main
module main (
  input  in_1,
  input  [1:0] in_2,
  input  in_3,
  input  in_4,
  input  in_5,
  input  in_6,
  input  in_7,
  input  in_8,
  input  in_9,
  input  [3:0] in_10,
  input  in_11,
  input  [2:0] in_12,
  input  in_13,
  input  in_14,
  input  in_15,
  input  [1:0] in_16,
  input  in_17,
  input  in_18,
  input  in_19,
  input  in_20,
  input  in_21,
  input  in_22
);

  wire clock_1_out;
  wire [7:0] counter_1_q;

  // Probe on in_2
  // Probe on in_10
  // Probe on in_12
  // Probe on in_16
  Counter #(.trigger("falling")) counter_1 (
    .count(1'b1), .Q(counter_1_q), .clk(clock_1_out));  // open: load, D, carry, clr
  Clock clock_1 (.out(clock_1_out));
  // Probe on {3'b000, in_22, in_21, in_20, in_19, in_18, in_17, in_16, in_15, in_14, in_13, in_12, in_11, in_10, in_9, in_8, in_7, in_6, in_5, in_4, in_3, in_2, in_1}
  RAM #(.dataWidth(32), .bus("separate")) ram_1 (
    .addr(counter_1_q),
    .din({3'b000, in_22, in_21, in_20, in_19, in_18, in_17, in_16, in_15, in_14, in_13, in_12, in_11, in_10, in_9, in_8, in_7, in_6, in_5, in_4, in_3, in_2, in_1}),
    .str(1'b1), .clk(clock_1_out));  // open: data, sel, ld, clr

  // Other names for the same wires on the sheet: BranchSlct = in_1; PCInSlct[1:0] = in_2; PCWE = in_3;
  //   InstRegWE = in_4; CLInSlct = in_5; CLWE = in_6; DspAInSlct = in_7; DspDInSlct = in_8; DspWE = in_9;
  //   TopOutOffset[3:0] = in_10; DAInSlct = in_11; DDInSlct[2:0] = in_12; MemWE = in_13; MemRE = in_14;
  //   ALUXWE = in_15; TopInSlct[1:0] = in_16; TopWE = in_17; BaseInSlct = in_18; BaseWE = in_19; MICInSlct = in_20;
  //   MICWE = in_21; OutputWE = in_22
endmodule
